# Fritzing sketch ArduinoEM (saved by Fritzing 0.9.3b)

parts:
  Arduino_Mega = Arduino Mega 2560 (Rev3)
  PART1 = CC3000 WiFi Breakout Board [part_number=WRL-12072]
  MQ-2_Breakout = Gas Sensor Breakout Board
  MQ-3_Breakout = Gas Sensor Breakout Board
  MQ-4_Breakout = Gas Sensor Breakout Board
  MQ-5_Breakout = Gas Sensor Breakout Board
  MQ-6_Breakout = Gas Sensor Breakout Board
  MQ-7_Breakout = Gas Sensor Breakout Board
  MQ-135_Breakout = Gas Sensor Breakout Board
  MQ-9_Breakout = Gas Sensor Breakout Board
  MQ-8_Breakout = Gas Sensor Breakout Board
  U1 = V_REG_LD1117VXX [package=78xxl]
  C2 = Electrolytic Capacitor [capacitance=0.22mF voltage=20V package="300 mil [THT, electrolytic]"]
  C3 = Capacitor [package=cap-pth-small]
  SI7021_breakout = Humidity Temperature Sensor SI7021
  ML8511_Breakout_Board = ML8511 UV Sensor Breakout [part_number=ML8511]
  Step_Down_SMPS = VERTER 5V USB Buck-Boost
  BMP180_Breakout = Barometric Pressure Sensor - BMP180 Breakout (GY-68)

nets:
  N1: Arduino_Mega.A8, MQ-135_Breakout.AOUT
  N2: Arduino_Mega.A9, ML8511_Breakout_Board.OUT
  N3: Arduino_Mega.A0, MQ-2_Breakout.AOUT
  N4: Arduino_Mega.A1, MQ-3_Breakout.AOUT
  N5: Arduino_Mega.A2, MQ-4_Breakout.AOUT
  N6: Arduino_Mega.A3, MQ-5_Breakout.AOUT
  N7: Arduino_Mega.A4, MQ-6_Breakout.AOUT
  N8: Arduino_Mega.A5, MQ-7_Breakout.AOUT
  N9: Arduino_Mega.A6, MQ-8_Breakout.AOUT
  N10: Arduino_Mega.A7, MQ-9_Breakout.AOUT
  N11: Arduino_Mega.D21/SCL, Arduino_Mega.D20/SDA, Arduino_Mega.SCL, Arduino_Mega.SDA, SI7021_breakout.SCL, BMP180_Breakout.SCL
  5V: Arduino_Mega.VIN, PART1.VCC, MQ-2_Breakout.5V, MQ-3_Breakout.5V, MQ-4_Breakout.5V, MQ-5_Breakout.5V, MQ-6_Breakout.5V, MQ-7_Breakout.5V, MQ-135_Breakout.5V, MQ-9_Breakout.5V, MQ-8_Breakout.5V, U1.IN, Step_Down_SMPS.5.0V
  N12: Arduino_Mega.D2_PWM, PART1.INT
  N13: Arduino_Mega.D50, PART1.MISO
  N14: Arduino_Mega.D51, PART1.MOSI
  N15: Arduino_Mega.D52, PART1.SCK
  N16: Arduino_Mega.D53, PART1.CS
  GND: PART1.GND, MQ-2_Breakout.GND, MQ-3_Breakout.GND, MQ-4_Breakout.GND, MQ-5_Breakout.GND, MQ-6_Breakout.GND, MQ-7_Breakout.GND, MQ-135_Breakout.GND, MQ-9_Breakout.GND, MQ-8_Breakout.GND, U1.GND, C2.-, C3.2, SI7021_breakout.GND, ML8511_Breakout_Board.GND, Step_Down_SMPS.GND, BMP180_Breakout.GND
  N17: U1.OUT, C3.1, ML8511_Breakout_Board.3.3V
  VCC: C2.+, SI7021_breakout.VCC, BMP180_Breakout.VCC
  N18: SI7021_breakout.SDA, BMP180_Breakout.SDA

custom parts:
  CC3000 WiFi Breakout Board: Breakout board for TI CC3000 WiFi module.
  Gas Sensor Breakout Board: Gas sensor breakout board. Input voltage is 5V. Sensor output is available in analog and digital.
  Humidity Temperature Sensor SI7021: SI7021 sensor breakout board.
  ML8511 UV Sensor Breakout: Description: The ML8511 breakout is an easy to use ultraviolet light sensor. The MP8511 UV Sensor works by outputing an analog signal in relation to the amount of UV light it detects. This breakout can be very handy in creating devices that warn the user of sunburn or detect the UV index as it relates to weather conditions. This sensor breakout can detect 280-390nm light most effectively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
  VERTER 5V USB Buck-Boost: VERTER can take battery voltages from 3-12VDC and output a nice 5V DC, which makes it a perfect universal power supply for your portable project! Where Verter really shines is when you have a battery or power range that can fluctuate a lot, or you don't know what you'll end up using.
