# Fritzing sketch INECC_IoT_v2 (saved by Fritzing 0.9.3b)
breadboards: 1

parts:
  WeMos_D1_Mini1 = WeMos D1 Mini
  DHT1 = DHT11 Humitidy and Temperature Sensor
  R1 = Resistor [tolerance=±5% resistance=10k package="0805 [SMD]"]
  Grove2 = Grove Dust Sensor
  Part1 = MQ-9 breakout

nets:
  N1: WeMos_D1_Mini1.A0, Part1.AO
  N2: WeMos_D1_Mini1.D1, Grove2.SIG
  N3: WeMos_D1_Mini1.D2, DHT1.DATA, R1.Pin_0
  VCC: DHT1.VDD, R1.Pin_1, Grove2.VCC, Part1.VCC
  GND: DHT1.GND, Grove2.GND, Part1.GND

custom parts:
  DHT11 Humitidy and Temperature Sensor: DHT11 Humidity and Temperature Sensor
  Grove Dust Sensor: PPD42 Grove Dust Sensor
  MQ-9 breakout: SKU: 101284
